# Fritzing sketch Fritzing_File (saved by Fritzing 0.9.3b)
breadboards: 1

parts:
  LCD1 = LCD screen
  Part1 = RFID-RC522-v2
  Part2 = BluePill
  Part3 = Arduino Uno (Rev3) - ICSP
  R1 = Resistor [tolerance=±5% resistance=220 package="2010 [SMD]"]
  R2 = Resistor [tolerance=±5% resistance=220 package="2010 [SMD]"]
  D2 = LTE-302 [package=lte-302]
  LED1 = LED - 3mm [color="Red (633nm)" package="3 mm [THT]"]
  U1 = POT [package=pot_alpha_rv16af-20]

nets:
  GND: LCD1.VSS, LCD1.R/W, LCD1.LED-, Part1.GND, Part2.GND, Part3.GND, R1.Pin_0, R2.Pin_0, U1.E
  N1: LCD1.VDD, LCD1.LED+, U1.A
  N2: LCD1.V0, U1.S
  N3: LCD1.RS, Part2.B1
  N4: LCD1.E, Part2.B0
  N5: LCD1.DB4, Part2.A4
  N6: LCD1.DB5, Part2.A5
  N7: LCD1.DB6, Part2.A6
  N8: LCD1.DB7, Part2.A7
  N9: Part1.SDA, Part3.D10_PWM/SS
  N10: Part1.SCK, Part3.D13/SCK
  N11: Part1.MOSI, Part3.D11_PWM/MOSI
  N12: Part1.MISO, Part3.ICSP_MISO, Part3.D12/MISO
  N13: Part1.RST, Part3.D9_PWM
  3.3V: Part1.3.3V, Part3.3V3
  N14: Part2.A12, LED1.anode
  N15: Part2.A11, D2.A
  N16: R1.Pin_1, LED1.cathode
  N17: R2.Pin_1, D2.C

notes:
  RFID MFRC522
  Arduino Uno
  STM32
  LCD 16*2
  BreadBoard
  POT
  Communication Protocol Lab

custom parts:
  RFID-RC522-v2: A simple China made RFID-RC522 Reader; do check the pin labels, as this is a MFRC522 based clone.
